// Logisim project CPU.circ as structural Verilog: 1 circuit, main circuit main
module main (
);

  // Register_File_main main_1: pin names not known
  // ALU_main main_2: pin names not known
endmodule
